# Fritzing sketch Hub-JeeNode (saved by Fritzing 0.7.12b)

parts:
  LED1 = LED - 3mm [color="Red (633nm)" package="3 mm [THT]"]
  R2 = Resistor [tolerance=±5% resistance=150 package=THT]
  Part1 = FTDI Basic Programmer
  Part2 = JeeNode wireless microcontroller
  PhotoTransistor1 = PhotoTransistor
  R3 = Resistor [tolerance=±5% resistance=100k package=THT]
  T1 = LM35 Temperature Sensor [package="TO92 [THT]"]
  D1 = Schottky Diode [part_number=1N5817 package="300 mil [THT]"]
  R4 = Resistor [tolerance=±5% resistance=18k package=THT]

nets (from the breadboard view):
  GND: LED1.cathode, Part1.GND, Part2.GND, D1.cathode, R4.Pin_1
  N1: LED1.anode, R2.Pin_1
  N2: R2.Pin_0, Part2.B1
  N3: Part1.DTR, Part2.DTR
  N4: Part1.RXI, Part2.TXD
  N5: Part1.TXO, Part2.RXD
  N6: Part1.POWER, Part2.PWX
  N7: Part1.CTS, Part2.N/C
  N8: Part2.VCC, R3.Pin_1, T1.+Vs
  N9: Part2.INT2, PhotoTransistor1.B, R3.Pin_0
  N10: Part2.A2, T1.GND, D1.anode
  N11: Part2.A3, T1.Vout, R4.Pin_0

custom parts:
  PhotoTransistor: A standard NPN-transistor
